// Logisim project V202300998_Project1_ALU_V3.circ as structural Verilog: 24 circuits, main circuit ALU32
module ALU32 (
  input  [3:0] Op,
  input  [31:0] B,
  input  [31:0] A,
  input  [4:0] Sa,
  output V,
  output [31:0] C
);

  wire [31:0] addsub32_1_c, comparator32_1_c, logical32_1_c, shifter32_1_c;

  AddSub32 addsub32_1 (.A(A), .B(B), .Op(Op), .V(V), .C(addsub32_1_c));
  Comparator32 comparator32_1 (.A(A), .B(B), .Op(Op), .C(comparator32_1_c));
  Logical32 logical32_1 (.A(A), .B(B), .Op(Op), .C(logical32_1_c));
  Shifter32 shifter32_1 (.B(B), .Sa(Sa), .Op(Op), .C(shifter32_1_c));
  assign C = addsub32_1_c | comparator32_1_c | logical32_1_c | shifter32_1_c;  // OR_Gate or_1, 32 bits wide

  // Notes on the sheet:
  //   Do not delete or rename any of the input or output pins, and do not add any other pins.
  //   (It's fine to move the pins around, though)
endmodule

module Add1 (
  input  A,
  input  B,
  input  Cin,
  output S,
  output Cout
);

  wire and_1_out, and_2_out, and_3_out, xor_1_out;

  xor xor_1 (xor_1_out, A, B);
  and and_1 (and_1_out, Cin, A);
  and and_2 (and_2_out, Cin, B);
  and and_3 (and_3_out, B, A);
  xor xor_2 (S, xor_1_out, Cin);
  or or_1 (Cout, and_1_out, and_2_out, and_3_out);
endmodule

module Add4 (
  input  [3:0] A,
  input  [3:0] B,
  input  Cin,
  output Cout,
  output [3:0] S
);

  wire add1_1_cout, add1_2_cout, add1_3_cout;

  Add1 add1_1 (.A(A[0]), .B(B[0]), .Cin(Cin), .S(S[0]), .Cout(add1_1_cout));
  Add1 add1_2 (.A(A[1]), .B(B[1]), .Cin(add1_1_cout), .S(S[1]), .Cout(add1_2_cout));
  Add1 add1_3 (.A(A[2]), .B(B[2]), .Cin(add1_2_cout), .S(S[2]), .Cout(add1_3_cout));
  Add1 add1_4 (.A(A[3]), .B(B[3]), .Cin(add1_3_cout), .S(S[3]), .Cout(Cout));
endmodule

module Add4V (
  input  [3:0] A,
  input  [3:0] B,
  input  Cin,
  output V,
  output [3:0] S
);

  wire add1_1_cout, add1_2_cout, add1_3_cout, add1_4_cout;

  Add1 add1_1 (.A(A[0]), .B(B[0]), .Cin(Cin), .S(S[0]), .Cout(add1_1_cout));
  Add1 add1_2 (.A(A[1]), .B(B[1]), .Cin(add1_1_cout), .S(S[1]), .Cout(add1_2_cout));
  Add1 add1_3 (.A(A[2]), .B(B[2]), .Cin(add1_2_cout), .S(S[2]), .Cout(add1_3_cout));
  Add1 add1_4 (.A(A[3]), .B(B[3]), .Cin(add1_3_cout), .S(S[3]), .Cout(add1_4_cout));
  xor xor_1 (V, add1_4_cout, add1_3_cout);

  // Notes on the sheet:
  //   (1)
endmodule

module Add16 (
  input  [15:0] A,
  input  [15:0] B,
  input  Cin,
  output Cout,
  output [15:0] S
);

  wire add4_1_cout, add4_2_cout, add4_3_cout;

  Add4 add4_1 (.A(A[3:0]), .B(B[3:0]), .Cin(Cin), .Cout(add4_1_cout), .S(S[3:0]));
  Add4 add4_2 (.A(A[7:4]), .B(B[7:4]), .Cin(add4_1_cout), .Cout(add4_2_cout), .S(S[7:4]));
  Add4 add4_3 (.A(A[11:8]), .B(B[11:8]), .Cin(add4_2_cout), .Cout(add4_3_cout), .S(S[11:8]));
  Add4 add4_4 (.A(A[15:12]), .B(B[15:12]), .Cin(add4_3_cout), .Cout(Cout), .S(S[15:12]));
endmodule

module Add16V (
  input  [15:0] A,
  input  [15:0] B,
  input  Cin,
  output V,
  output [15:0] S
);

  wire add4_1_cout, add4_2_cout, add4_3_cout;

  Add4 add4_1 (.A(A[3:0]), .B(B[3:0]), .Cin(Cin), .Cout(add4_1_cout), .S(S[3:0]));
  Add4 add4_2 (.A(A[7:4]), .B(B[7:4]), .Cin(add4_1_cout), .Cout(add4_2_cout), .S(S[7:4]));
  Add4 add4_3 (.A(A[11:8]), .B(B[11:8]), .Cin(add4_2_cout), .Cout(add4_3_cout), .S(S[11:8]));
  Add4V add4v_1 (.A(A[15:12]), .B(B[15:12]), .Cin(add4_3_cout), .V(V), .S(S[15:12]));
endmodule

module Add32 (
  input  [31:0] A,
  input  [31:0] B,
  input  Cin,
  output V,
  output [31:0] C
);

  wire add16_1_cout;

  Add16 add16_1 (.A(A[15:0]), .B(B[15:0]), .Cin(Cin), .Cout(add16_1_cout), .S(C[15:0]));
  Add16V add16v_1 (.A(A[31:16]), .B(B[31:16]), .Cin(add16_1_cout), .V(V), .S(C[31:16]));

  // Notes on the sheet:
  //   Do not delete or rename any of the input or output pins, and do not add any other pins.
  //   (It's fine to move the pins around, though)
endmodule

module AddSub32 (
  input  [31:0] A,
  input  [31:0] B,
  input  [3:0] Op,
  output V,
  output [31:0] C
);

  wire and_1_out, and_2_out, not_1_out, not_2_out, not_3_out, or_1_out;
  wire [31:0] add32_1_c, multiplexer_1_out, not_4_out;

  not not_1 (not_1_out, Op[2]);
  not not_2 (not_2_out, Op[3]);
  not not_3 (not_3_out, Op[1]);
  and and_1 (and_1_out, Op[1], not_1_out, not_2_out);
  and and_2 (and_2_out, Op[1], Op[2], not_2_out);
  assign not_4_out = ~B;  // NOT_Gate not_4, 32 bits wide
  or or_1 (or_1_out, and_1_out, and_2_out);
  Multiplexer #(.width(32)) multiplexer_1 (
    .in0(B), .in1(not_4_out), .out(multiplexer_1_out), .sel(and_2_out), .en(or_1_out));
  Add32 add32_1 (.A(A), .B(multiplexer_1_out), .Cin(and_2_out), .V(V), .C(add32_1_c));
  Multiplexer #(.width(32)) multiplexer_2 (.in1(add32_1_c), .out(C), .sel(or_1_out), .en(or_1_out));  // open: in0

  // Notes on the sheet:
  //   (1)
  //   (2)
  //   (1)
  //   (2)
endmodule

module LeftShift1 (
  input  Cin,
  input  [31:0] B,
  output [31:0] C
);


  assign C = {B[30:0], Cin};
endmodule

module LeftShift2 (
  input  Cin,
  input  [31:0] B,
  output [31:0] C
);

  wire [31:0] leftshift1_1_c;

  LeftShift1 leftshift1_1 (.Cin(Cin), .B(B), .C(leftshift1_1_c));
  LeftShift1 leftshift1_2 (.Cin(Cin), .B(leftshift1_1_c), .C(C));
endmodule

module LeftShift4 (
  input  Cin,
  input  [31:0] B,
  output [31:0] C
);

  wire [31:0] leftshift2_1_c;

  LeftShift2 leftshift2_1 (.Cin(Cin), .B(B), .C(leftshift2_1_c));
  LeftShift2 leftshift2_2 (.Cin(Cin), .B(leftshift2_1_c), .C(C));
endmodule

module LeftShift8 (
  input  Cin,
  input  [31:0] B,
  output [31:0] C
);

  wire [31:0] leftshift4_1_c;

  LeftShift4 leftshift4_1 (.Cin(Cin), .B(B), .C(leftshift4_1_c));
  LeftShift4 leftshift4_2 (.Cin(Cin), .B(leftshift4_1_c), .C(C));
endmodule

module LeftShift16 (
  input  Cin,
  input  [31:0] B,
  output [31:0] C
);

  wire [31:0] leftshift8_1_c;

  LeftShift8 leftshift8_1 (.Cin(Cin), .B(B), .C(leftshift8_1_c));
  LeftShift8 leftshift8_2 (.Cin(Cin), .B(leftshift8_1_c), .C(C));
endmodule

module LeftShift32 (
  input  Cin,
  input  [31:0] B,
  input  [4:0] Sa,
  output [31:0] C
);

  wire [31:0] leftshift1_1_c, leftshift2_1_c, leftshift4_1_c, leftshift8_1_c, leftshift16_1_c,
       multiplexer_1_out, multiplexer_2_out, multiplexer_3_out, multiplexer_4_out;

  LeftShift1 leftshift1_1 (.Cin(Cin), .B(B), .C(leftshift1_1_c));
  Multiplexer #(.width(32), .enable("false")) multiplexer_1 (
    .in0(B), .in1(leftshift1_1_c), .out(multiplexer_1_out), .sel(Sa[0]));
  LeftShift2 leftshift2_1 (.Cin(Cin), .B(multiplexer_1_out), .C(leftshift2_1_c));
  Multiplexer #(.width(32), .enable("false")) multiplexer_2 (
    .in0(multiplexer_1_out), .in1(leftshift2_1_c), .out(multiplexer_2_out), .sel(Sa[1]));
  LeftShift4 leftshift4_1 (.Cin(Cin), .B(multiplexer_2_out), .C(leftshift4_1_c));
  Multiplexer #(.width(32), .enable("false")) multiplexer_3 (
    .in0(multiplexer_2_out), .in1(leftshift4_1_c), .out(multiplexer_3_out), .sel(Sa[2]));
  LeftShift8 leftshift8_1 (.Cin(Cin), .B(multiplexer_3_out), .C(leftshift8_1_c));
  Multiplexer #(.width(32), .enable("false")) multiplexer_4 (
    .in0(multiplexer_3_out), .in1(leftshift8_1_c), .out(multiplexer_4_out), .sel(Sa[3]));
  LeftShift16 leftshift16_1 (.Cin(Cin), .B(multiplexer_4_out), .C(leftshift16_1_c));
  Multiplexer #(.width(32), .enable("false")) multiplexer_5 (
    .in0(multiplexer_4_out), .in1(leftshift16_1_c), .out(C), .sel(Sa[4]));

  // Notes on the sheet:
  //   (1)
  //   Do not delete or rename any of the input or output pins, and do not add any other pins.
  //   (It's fine to move them around, though)
  //   (2)
  //   (3)
  //   (4)
  //   (5)
endmodule

module Reverse32 (
  input  [31:0] B,
  output [31:0] C
);


  assign C = {B[0], B[1], B[2], B[3], B[4], B[5], B[6], B[7], B[8], B[9], B[10], B[11], B[12], B[13], B[14], B[15], B[16], B[17], B[18], B[19], B[20], B[21], B[22], B[23], B[24], B[25], B[26], B[27], B[28], B[29], B[30], B[31]};
endmodule

module MSB (
  input  [31:0] A,
  output B
);


  assign B = A[31];
endmodule

module Shifter32 (
  input  [31:0] B,
  input  [4:0] Sa,
  input  [3:0] Op,
  output [31:0] C
);

  wire and_1_out, and_4_out, msb_1_b, not_1_out, not_2_out, not_3_out, not_4_out, or_1_out;
  wire [1:0] and_2_out;
  wire [31:0] leftshift32_1_c, multiplexer_1_out, reverse32_1_c, reverse32_2_c;

  not not_1 (not_1_out, Op[3]);
  not not_2 (not_2_out, Op[2]);
  not not_3 (not_3_out, Op[0]);
  not not_4 (not_4_out, Op[1]);
  Reverse32 reverse32_1 (.B(B), .C(reverse32_1_c));
  and and_1 (and_1_out, not_4_out, not_2_out, not_1_out);
  and and_2 (and_2_out[0], not_3_out, not_4_out, Op[2], Op[3]);
  and and_3 (and_2_out[1], Op[0], not_4_out, Op[2], Op[3]);
  or or_1 (or_1_out, and_1_out, and_2_out[0], and_2_out[1]);
  Multiplexer #(.select(2), .width(32)) multiplexer_1 (
    .in0(B), .in1(reverse32_1_c), .in2(reverse32_1_c), .out(multiplexer_1_out), .sel(and_2_out), .en(or_1_out));  // open: in3
  MSB msb_1 (.A(B), .B(msb_1_b));
  and and_4 (and_4_out, msb_1_b, and_2_out[1]);
  LeftShift32 leftshift32_1 (.Cin(and_4_out), .B(multiplexer_1_out), .Sa(Sa), .C(leftshift32_1_c));
  Reverse32 reverse32_2 (.B(leftshift32_1_c), .C(reverse32_2_c));
  Multiplexer #(.select(2), .width(32)) multiplexer_2 (
    .in0(leftshift32_1_c), .in1(reverse32_2_c), .in2(reverse32_2_c), .out(C), .sel(and_2_out), .en(or_1_out));  // open: in3

  // Notes on the sheet:
  //   (1)
  //   (2)
  //   (3)
  //   (4)
  //   (1)
  //   (1)
  //   (2)
  //   (2)
endmodule

module Logical32 (
  input  [31:0] A,
  input  [31:0] B,
  input  [3:0] Op,
  output [31:0] C
);

  wire and_2_out, and_3_out, and_4_out, and_5_out, not_1_out, not_2_out, not_3_out, not_4_out, or_4_out;
  wire [1:0] or_2_out;
  wire [31:0] and_1_out, nor_1_out, or_1_out, xor_1_out;

  not not_1 (not_1_out, Op[3]);
  not not_2 (not_2_out, Op[2]);
  not not_3 (not_3_out, Op[1]);
  not not_4 (not_4_out, Op[0]);
  assign and_1_out = A & B;  // AND_Gate and_1, 32 bits wide
  assign or_1_out = A | B;  // OR_Gate or_1, 32 bits wide
  and and_2 (and_2_out, Op[0], not_3_out, Op[2], not_1_out);
  and and_3 (and_3_out, Op[0], Op[1], not_2_out, Op[3]);
  and and_4 (and_4_out, not_4_out, Op[1], not_2_out, Op[3]);
  and and_5 (and_5_out, not_4_out, not_3_out, Op[2], not_1_out);
  assign xor_1_out = A ^ B;  // XOR_Gate xor_1, 32 bits wide
  assign nor_1_out = ~(A | B);  // NOR_Gate nor_1, 32 bits wide
  or or_2 (or_2_out[0], and_2_out, and_3_out);
  or or_3 (or_2_out[1], and_3_out, and_4_out);
  or or_4 (or_4_out, and_2_out, and_3_out, and_4_out, and_5_out);
  Multiplexer #(.select(2), .width(32)) multiplexer_1 (
    .in0(and_1_out), .in1(or_1_out), .in2(xor_1_out), .in3(nor_1_out), .out(C), .sel(or_2_out), .en(or_4_out));

  // Notes on the sheet:
  //   (1)
  //   (2)
  //   (3)
  //   (4)
  //   (1)
  //   (2)
  //   (3)
endmodule

module Comparator32 (
  input  [31:0] A,
  input  [31:0] B,
  input  [3:0] Op,
  output [31:0] C
);

  wire and_1_out, and_2_out, and_3_out, and_4_out, greaterthan0_1_o, isequal_1_o, lessthanorequal0_1_o,
       not_1_out, not_2_out, not_3_out, not_4_out, not_5_out, or_1_out;
  wire [1:0] or_2_out;
  wire [31:0] bitextend1to32_1_b, bitextend1to32_2_b, bitextend1to32_3_b, bitextend1to32_4_b;

  not not_1 (not_1_out, Op[3]);
  IsEqual isequal_1 (.A(A), .B(B), .O(isequal_1_o));
  not not_2 (not_2_out, Op[1]);
  not not_3 (not_3_out, Op[2]);
  not not_4 (not_4_out, isequal_1_o);
  LessThanOrEqual0 lessthanorequal0_1 (.A(A), .O(lessthanorequal0_1_o));
  GreaterThan0 greaterthan0_1 (.A(A), .O(greaterthan0_1_o));
  not not_5 (not_5_out, Op[0]);
  and and_1 (and_1_out, not_5_out, not_2_out, not_3_out, Op[3]);
  and and_2 (and_2_out, Op[0], not_2_out, not_3_out, Op[3]);
  and and_3 (and_3_out, not_5_out, Op[1], Op[2], Op[3]);
  and and_4 (and_4_out, Op[0], Op[1], Op[2], Op[3]);
  BitExtend1to32 bitextend1to32_1 (.A(not_4_out), .B(bitextend1to32_1_b));
  BitExtend1to32 bitextend1to32_2 (.A(isequal_1_o), .B(bitextend1to32_2_b));
  BitExtend1to32 bitextend1to32_3 (.A(lessthanorequal0_1_o), .B(bitextend1to32_3_b));
  BitExtend1to32 bitextend1to32_4 (.A(greaterthan0_1_o), .B(bitextend1to32_4_b));
  or or_1 (or_1_out, and_1_out, and_2_out, and_3_out, and_4_out);
  or or_2 (or_2_out[0], and_2_out, and_4_out);
  or or_3 (or_2_out[1], and_3_out, and_4_out);
  Multiplexer #(.select(2), .width(32)) multiplexer_1 (
    .in0(bitextend1to32_1_b), .in1(bitextend1to32_2_b), .in2(bitextend1to32_3_b), .in3(bitextend1to32_4_b),
    .out(C), .sel(or_2_out), .en(or_1_out));

  // Notes on the sheet:
  //   (1)
  //   (2)
  //   (3)
  //   (4)
  //   (1)
  //   (2)
  //   (3)
  //   (4)
  //   (1)
  //   (2)
  //   (3)
endmodule

module IsEqual (
  input  [31:0] A,
  input  [31:0] B,
  output O
);

  wire [31:0] xor_1_out;

  assign xor_1_out = A ^ B;  // XOR_Gate xor_1, 32 bits wide
  IsEqual0 isequal0_1 (.A(xor_1_out), .O(O));
endmodule

module BitExtend1to32 (
  input  A,
  output [31:0] B
);


  assign B = {{31{1'b0}}, A};
endmodule

module IsEqual0 (
  input  [31:0] A,
  output O
);

  wire or_3_out;
  wire [1:0] or_2_out;
  wire [7:0] or_1_out;

  assign or_1_out = A[7:0] | A[15:8] | A[23:16] | A[31:24];  // OR_Gate or_1, 8 bits wide
  assign or_2_out = or_1_out[1:0] | or_1_out[3:2] | or_1_out[5:4] | or_1_out[7:6];  // OR_Gate or_2, 2 bits wide
  or or_3 (or_3_out, or_2_out[0], or_2_out[1]);
  not not_1 (O, or_3_out);

  // Notes on the sheet:
  //   (1)
  //   (2)
  //   (3)
endmodule

module LessThanOrEqual0 (
  input  [31:0] A,
  output O
);

  wire isequal0_1_o, msb_1_b;

  MSB msb_1 (.A(A), .B(msb_1_b));
  IsEqual0 isequal0_1 (.A(A), .O(isequal0_1_o));
  or or_1 (O, msb_1_b, isequal0_1_o);
endmodule

module GreaterThan0 (
  input  [31:0] A,
  output O
);

  wire isequal0_1_o, msb_1_b, not_1_out, not_2_out;

  MSB msb_1 (.A(A), .B(msb_1_b));
  not not_1 (not_1_out, msb_1_b);
  IsEqual0 isequal0_1 (.A(A), .O(isequal0_1_o));
  not not_2 (not_2_out, isequal0_1_o);
  and and_1 (O, not_1_out, not_2_out);
endmodule
